# Fritzing sketch fritzing (saved by Fritzing 0.9.3b)
breadboards: 2

parts:
  Part1 = Arduino Nano (Rev3.0) (ICSP)
  U1 = ESP8266 NodeMCU LoLin module
  LED1 = RGB LED (com. cathode, rgb) [package="5 mm [THT]"]
  S1 = Pushbutton [package="[THT]"]
  R1 = Resistor [tolerance=±5% resistance=220 package="0603 [SMD]"]
  R2 = Resistor [tolerance=±5% resistance=220 package="0603 [SMD]"]
  R3 = Resistor [tolerance=±5% resistance=220 package="0603 [SMD]"]
  JP1 = Header 4 [package=jst-4-pth]
  VCC1 = Battery

nets:
  GND: Part1.GND, U1.GND, S1.Pin_3, S1.Pin_4, JP1.3, JP1.4, VCC1.-
  N1: Part1.D3, R1.Pin_1
  N2: Part1.D5, R2.Pin_1
  N3: Part1.D6, R3.Pin_1
  N4: Part1.D7, S1.Pin_1, S1.Pin_2
  N5: Part1.D8, U1.TX
  N6: Part1.D9, U1.RX
  VIN: Part1.VIN, U1.Vin, VCC1.+
  N7: Part1.5V, LED1.common_cathode, JP1.2
  N8: Part1.A0, JP1.1
  N9: LED1.red_anode, R1.Pin_0
  N10: LED1.green_anode, R2.Pin_0
  N11: LED1.blue_anode, R3.Pin_0

notes:
  DFRobot TS01 Non-contact IR Temperature Sensor

custom parts:
  ESP8266 NodeMCU LoLin module: ESP8266 based NodeMCU
